// Logisim project control-logic.circ as structural Verilog: 1 circuit, main circuit control_logic
module control_logic (
  input  [31:0] Instruction,
  input  BrEq,
  input  BrLt,
  output PCSel,
  output RegWEn,
  output [2:0] ImmSel,
  output BrUn,
  output ASel,
  output BSel,
  output [3:0] ALUSel,
  output MemWEn,
  output [1:0] WBSel
);

  wire Add, addi, and_1_out, and_2_out, and_3_out, and_4_out, and_5_out, and_6_out, and_op, andi, beq, bge,
       bgeu, blt, bltu, bne, Btype, F3_0, F3_1, F3_2, F3_3, F3_4, F3_5, F3_6, F3_7, F7_00, F7_01, F7_20,
       Itype03, Itype13, Itype67, jarl, Jtype, lb, lh, lw, Mul, mulh, mulhu, not_1_out, not_2_out, not_3_out,
       or_op, ori, Rtype, sb, sh, sll_op, slli, slt, slti, sra_op, srai, srl_op, srli, Stype, Sub, sw,
       Utype17, Utype37, xor_op, xori;
  wire [5:0] ROMinput;
  wire [15:14] rom_1_data;

  Comparator #(.width(7)) comparator_1 (.a(Instruction[6:0]), .b(7'b0110011), .eq(Rtype));  // open: gt, lt
  Comparator #(.width(7)) comparator_2 (.a(Instruction[6:0]), .b(7'b0000011), .eq(Itype03));  // open: gt, lt
  Comparator #(.width(7)) comparator_3 (.a(Instruction[6:0]), .b(7'b0010011), .eq(Itype13));  // open: gt, lt
  Comparator #(.width(7)) comparator_4 (.a(Instruction[6:0]), .b(7'b0100011), .eq(Stype));  // open: gt, lt
  Comparator #(.width(7)) comparator_5 (.a(Instruction[6:0]), .b(7'b1100011), .eq(Btype));  // open: gt, lt
  Comparator #(.width(7)) comparator_6 (.a(Instruction[6:0]), .b(7'b0010111), .eq(Utype17));  // open: gt, lt
  Comparator #(.width(7)) comparator_7 (.a(Instruction[6:0]), .b(7'b0110111), .eq(Utype37));  // open: gt, lt
  Comparator #(.width(7)) comparator_8 (.a(Instruction[6:0]), .b(7'b1101111), .eq(Jtype));  // open: gt, lt
  Comparator #(.width(7)) comparator_9 (.a(Instruction[6:0]), .b(7'b1100111), .eq(Itype67));  // open: gt, lt
  ROM #(.addrWidth(6), .dataWidth(16)) rom_1 (
    .addr(ROMinput), .data({rom_1_data, WBSel, MemWEn, ALUSel, BSel, ASel, BrUn, ImmSel, RegWEn}));
  Comparator #(.mode("unsigned"), .width(3)) comparator_10 (
    .a(Instruction[14:12]), .b(3'b000), .eq(F3_0));  // open: gt, lt
  Comparator #(.mode("unsigned"), .width(3)) comparator_11 (
    .a(Instruction[14:12]), .b(3'b001), .eq(F3_1));  // open: gt, lt
  Comparator #(.mode("unsigned"), .width(3)) comparator_12 (
    .a(Instruction[14:12]), .b(3'b010), .eq(F3_2));  // open: gt, lt
  Comparator #(.mode("unsigned"), .width(3)) comparator_13 (
    .a(Instruction[14:12]), .b(3'b011), .eq(F3_3));  // open: gt, lt
  Comparator #(.mode("unsigned"), .width(3)) comparator_14 (
    .a(Instruction[14:12]), .b(3'b100), .eq(F3_4));  // open: gt, lt
  Comparator #(.mode("unsigned"), .width(3)) comparator_15 (
    .a(Instruction[14:12]), .b(3'b101), .eq(F3_5));  // open: gt, lt
  Comparator #(.mode("unsigned"), .width(3)) comparator_16 (
    .a(Instruction[14:12]), .b(3'b110), .eq(F3_6));  // open: gt, lt
  Comparator #(.mode("unsigned"), .width(3)) comparator_17 (
    .a(Instruction[14:12]), .b(3'b111), .eq(F3_7));  // open: gt, lt
  Comparator #(.width(7)) comparator_18 (.a(Instruction[31:25]), .b({7{1'b0}}), .eq(F7_00));  // open: gt, lt
  Comparator #(.width(7)) comparator_19 (.a(Instruction[31:25]), .b(7'b0000001), .eq(F7_01));  // open: gt, lt
  Comparator #(.width(7)) comparator_20 (.a(Instruction[31:25]), .b(7'b0100000), .eq(F7_20));  // open: gt, lt
  not not_1 (not_1_out, BrEq);
  not not_2 (not_2_out, BrLt);
  not not_3 (not_3_out, BrLt);
  and and_1 (and_1_out, beq, BrEq);
  and and_2 (and_2_out, bne, not_1_out);
  and and_3 (and_3_out, blt, BrLt);
  and and_4 (and_4_out, bge, not_2_out);
  and and_5 (and_5_out, bltu, BrLt);
  and and_6 (and_6_out, bgeu, not_3_out);
  or or_1 (PCSel, Jtype, and_1_out, and_2_out, and_3_out, and_4_out, and_5_out, and_6_out, jarl);
  and and_7 (Add, Rtype, F3_0, F7_00);
  and and_8 (Mul, Rtype, F3_0, F7_01);
  and and_9 (Sub, Rtype, F3_0, F7_20);
  and and_10 (sll_op, Rtype, F3_1, F7_00);
  and and_11 (mulh, Rtype, F3_1, F7_01);
  and and_12 (mulhu, Rtype, F3_3, F7_01);
  and and_13 (slt, Rtype, F3_2, F7_00);
  and and_14 (xor_op, Rtype, F3_4, F7_00);
  and and_15 (srl_op, Rtype, F3_5, F7_00);
  and and_16 (sra_op, Rtype, F3_5, F7_20);
  and and_17 (or_op, Rtype, F3_6, F7_00);
  and and_18 (and_op, Rtype, F3_7, F7_00);
  and and_19 (lb, Itype03, F3_0);
  and and_20 (lh, Itype03, F3_1);
  and and_21 (lw, Itype03, F3_2);
  and and_22 (addi, Itype13, F3_0);
  and and_23 (andi, Itype13, F3_7);
  and and_24 (ori, Itype13, F3_6);
  and and_25 (xori, Itype13, F3_4);
  and and_26 (slli, Itype13, F3_1, F7_00);
  and and_27 (srli, Itype13, F3_5, F7_00);
  and and_28 (srai, Itype13, F3_5, F7_20);
  and and_29 (slti, Itype13, F3_2);
  Priority_Encoder #(.select_enc(6)) priority_encoder_1 (
    .in0(Add), .in1(Mul), .in2(Sub), .in3(sll_op), .in4(mulh), .in5(mulhu), .in6(slt), .in7(xor_op),
    .in8(srl_op), .in9(sra_op), .in10(or_op), .in11(and_op), .in12(lb), .in13(lh), .in14(lw), .in15(addi),
    .in16(slli), .in17(slti), .in18(xori), .in19(srli), .in20(srai), .in21(ori), .in22(andi), .in23(sb),
    .in24(sh), .in25(sw), .in26(beq), .in27(bne), .in28(blt), .in29(bge), .in30(bltu), .in31(bgeu),
    .in32(Utype17), .in33(Utype37), .in34(Jtype), .in35(jarl), .out(ROMinput));  // open: in36, in37, in38, in39, in40, in41, in42, in43, in44, in45, in46, in47, in48, in49, in50, in51, in52, in53, in54, in55, in56, in57, in58, in59, in60, in61, in62, in63, gs, en_out, en_in
  and and_30 (sb, Stype, F3_0);
  and and_31 (sh, Stype, F3_1);
  and and_32 (sw, Stype, F3_2);
  and and_33 (beq, Btype, F3_0);
  and and_34 (bne, Btype, F3_1);
  and and_35 (blt, Btype, F3_4);
  and and_36 (bge, Btype, F3_5);
  and and_37 (bltu, Btype, F3_6);
  and and_38 (bgeu, Btype, F3_7);
  and and_39 (jarl, Itype67, F3_0);

  // Other names for the same wires on the sheet: Opcode[6:0] = Instruction[6:0]; Funct3[2:0] = Instruction[14:12];
  //   Funct7[6:0] = Instruction[31:25]

  // Notes on the sheet:
  //   INPUTS to your circuit
  //   Connect ROM Input here ->
  //   contents of rom_1 (hex, n*v repeats v):
  //   1001 1401 1601 1081 1481 1581 1101 1201 1281 1681 1301 1381 41 41 41 1041 10c1 1141 1241 12c1 16c1
  //   1341 13c1 842 842 842 4*64 74 1074 1067 17c7 2069 2041
  //   ROM FOR CONTROL LOGIC
  //   DON'T CHANGE THE LOCATIONS OF THE INPUTS AND OUTPUTS!
  //   This is only if you choose to do the ROM option
  //   CONNECT
  //   WIRE
  //   TO
  //   USE
  //   ROM
  //   OUTPUT from your circuit
  //   Reminder: If using ROM, use combinational logic for PCSel
endmodule
