// Logisim project partial-store.circ as structural Verilog: 1 circuit, main circuit partial_store
module partial_store (
  input  [31:0] Instruction,
  input  [31:0] MemAddress,
  input  [31:0] DataFromReg,
  input  MemWEn,
  output [3:0] MemWriteMask,
  output [31:0] DataToMem
);

  wire comparator_1_eq, StoreAndWrite;
  wire [3:0] multiplexer_1_out, multiplexer_2_out, multiplexer_3_out, multiplexer_7_out;
  wire [31:0] multiplexer_4_out, multiplexer_5_out, multiplexer_6_out, multiplexer_8_out;

  Comparator #(.width(7)) comparator_1 (.a(Instruction[6:0]), .b(7'b0100011), .eq(comparator_1_eq));  // open: gt, lt
  and and_1 (StoreAndWrite, comparator_1_eq, MemWEn);
  Multiplexer #(.select(2), .width(4)) multiplexer_1 (
    .in0(4'b0001), .in1(4'b0010), .in2(4'b0100), .in3(4'b1000), .out(multiplexer_1_out), .sel(MemAddress[1:0]));
  Multiplexer #(.select(2), .width(4)) multiplexer_2 (
    .in0(4'b0011), .in2(4'b1100), .out(multiplexer_2_out), .sel(MemAddress[1:0]));  // open: in1, in3
  Multiplexer #(.select(2), .width(4)) multiplexer_3 (
    .in0(4'b1111), .out(multiplexer_3_out), .sel(MemAddress[1:0]));  // open: in1, in2, in3
  Multiplexer #(.select(2), .width(32)) multiplexer_4 (
    .in0({{24{1'b0}}, DataFromReg[7:0]}), .in1({{16{1'b0}}, DataFromReg[7:0], {8{1'b0}}}),
    .in2({{8{1'b0}}, DataFromReg[7:0], {16{1'b0}}}), .in3({DataFromReg[7:0], {24{1'b0}}}),
    .out(multiplexer_4_out), .sel(MemAddress[1:0]));
  Multiplexer #(.select(2), .width(32)) multiplexer_5 (
    .in0({{16{1'b0}}, DataFromReg[15:0]}), .in2({DataFromReg[15:0], {16{1'b0}}}), .out(multiplexer_5_out),
    .sel(MemAddress[1:0]));  // open: in1, in3
  Multiplexer #(.select(2), .width(32)) multiplexer_6 (
    .in0(DataFromReg), .out(multiplexer_6_out), .sel(MemAddress[1:0]));  // open: in1, in2, in3
  Multiplexer #(.select(3), .width(4)) multiplexer_7 (
    .in0(multiplexer_1_out), .in1(multiplexer_2_out), .in2(multiplexer_3_out), .out(multiplexer_7_out),
    .sel(Instruction[14:12]));  // open: in3, in4, in5, in6, in7
  Multiplexer #(.select(3), .width(32)) multiplexer_8 (
    .in0(multiplexer_4_out), .in1(multiplexer_5_out), .in2(multiplexer_6_out), .out(multiplexer_8_out),
    .sel(Instruction[14:12]));  // open: in3, in4, in5, in6, in7
  Multiplexer #(.width(4)) multiplexer_9 (
    .in0(4'b0000), .in1(multiplexer_7_out), .out(MemWriteMask), .sel(StoreAndWrite));
  Multiplexer #(.width(32)) multiplexer_10 (
    .in0({32{1'b0}}), .in1(multiplexer_8_out), .out(DataToMem), .sel(StoreAndWrite));

  // Other names for the same wires on the sheet: byte0[7:0] = DataFromReg[7:0]; byte1[7:0] = DataFromReg[15:8];
  //   byte2[7:0] = DataFromReg[23:16]; byte3[7:0] = DataFromReg[31:24]; OPCode[6:0] = Instruction[6:0];
  //   F3[2:0] = Instruction[14:12]; addr[1:0] = MemAddress[1:0]

  // Notes on the sheet:
  //   INPUTS to your circuit
  //   DON'T CHANGE THE LOCATIONS OF THE INPUTS AND OUTPUTS!
  //   OUTPUT from your circuit
endmodule
