// Logisim project ex2.circ as structural Verilog: 6 circuits, main circuit AND2
module AND2 (
  input  A,
  input  B,
  output RESULT
);

  and and_1 (RESULT, A, B);

  // Notes on the sheet:
  //   Sample Circuit
endmodule

module NAND2 (
  input  A,
  input  B,
  output RESULT
);

  wire and_1_out;

  and and_1 (and_1_out, A, B);
  not not_1 (RESULT, and_1_out);
endmodule

module NOR2 (
  input  A,
  input  B,
  output RESULT
);

  wire or_1_out;

  or or_1 (or_1_out, A, B);
  not not_1 (RESULT, or_1_out);
endmodule

module XOR2 (
  input  A,
  input  B,
  output RESULT
);

  wire and_1_out, and_2_out, not_1_out, not_2_out;

  not not_1 (not_1_out, A);
  not not_2 (not_2_out, B);
  and and_1 (and_1_out, not_1_out, B);
  and and_2 (and_2_out, A, not_2_out);
  or or_1 (RESULT, and_1_out, and_2_out);
endmodule

module MUX2 (
  input  A,
  input  B,
  input  SEL,
  output RESULT
);

  wire and_1_out, and_2_out, not_1_out;

  not not_1 (not_1_out, SEL);
  and and_1 (and_1_out, A, not_1_out);
  and and_2 (and_2_out, B, SEL);
  or or_1 (RESULT, and_1_out, and_2_out);
endmodule

module MUX4 (
  input  A,
  input  B,
  input  C,
  input  D,
  input  SEL0,
  input  SEL1,
  output RESULT
);

  wire and_1_out, and_2_out, and_3_out, and_4_out, not_1_out, not_2_out, not_3_out, not_4_out;

  not not_1 (not_1_out, SEL0);
  not not_2 (not_2_out, SEL1);
  not not_3 (not_3_out, SEL1);
  not not_4 (not_4_out, SEL0);
  and and_1 (and_1_out, A, not_1_out, not_2_out);
  and and_2 (and_2_out, B, SEL0, not_3_out);
  and and_3 (and_3_out, D, SEL0, SEL1);
  and and_4 (and_4_out, C, not_4_out, SEL1);
  or or_1 (RESULT, and_1_out, and_2_out, and_4_out, and_3_out);
endmodule
