// Logisim project ex4.circ as structural Verilog: 5 circuits, main circuit RotRight
module RotRight (
  input  [15:0] INPUT0,
  input  [3:0] AMOUNT,
  output [15:0] OUTPUT0
);

  wire [15:0] multiplexer_1_out, multiplexer_2_out, multiplexer_3_out, rot1_1_out_2, rot2_1_out_2,
       rot4_1_out_2, rot4_2_out_2, rot4_3_out_2;

  rot4 rot4_1 (.out_2(rot4_1_out_2), .in_1(INPUT0));
  rot4 rot4_2 (.out_2(rot4_2_out_2), .in_1(rot4_1_out_2));
  Multiplexer #(.width(16)) multiplexer_1 (.in0(INPUT0), .in1(rot4_2_out_2), .out(multiplexer_1_out), .sel(AMOUNT[3]));
  Multiplexer #(.width(16)) multiplexer_2 (
    .in0(multiplexer_1_out), .in1(rot4_3_out_2), .out(multiplexer_2_out), .sel(AMOUNT[2]));
  rot4 rot4_3 (.out_2(rot4_3_out_2), .in_1(multiplexer_1_out));
  rot2 rot2_1 (.out_2(rot2_1_out_2), .in_1(multiplexer_2_out));
  Multiplexer #(.width(16)) multiplexer_3 (
    .in0(multiplexer_2_out), .in1(rot2_1_out_2), .out(multiplexer_3_out), .sel(AMOUNT[1]));
  Multiplexer #(.width(16)) multiplexer_4 (.in0(multiplexer_3_out), .in1(rot1_1_out_2), .out(OUTPUT0), .sel(AMOUNT[0]));
  rot1 rot1_1 (.out_2(rot1_1_out_2), .in_1(multiplexer_3_out));

  // Other names for the same wires on the sheet: b0 = AMOUNT[0]; b1 = AMOUNT[1]; b2 = AMOUNT[2]; b3 = AMOUNT[3]
endmodule

module rot1 (
  input  [15:0] in_1,
  output [15:0] out_2
);


  assign out_2 = {in_1[0], in_1[15:1]};
endmodule

module rot2 (
  input  [15:0] in_1,
  output [15:0] out_2
);

  wire [15:0] rot1_1_out_2;

  rot1 rot1_1 (.out_2(rot1_1_out_2), .in_1(in_1));
  rot1 rot1_2 (.out_2(out_2), .in_1(rot1_1_out_2));
endmodule

module rot4 (
  input  [15:0] in_1,
  output [15:0] out_2
);

  wire [15:0] rot2_1_out_2;

  rot2 rot2_1 (.out_2(rot2_1_out_2), .in_1(in_1));
  rot2 rot2_2 (.out_2(out_2), .in_1(rot2_1_out_2));
endmodule

module rot8 (
  input  [15:0] in_1,
  output [15:0] out_2
);

  wire [15:0] rot4_1_out_2;

  rot4 rot4_1 (.out_2(rot4_1_out_2), .in_1(in_1));
  rot4 rot4_2 (.out_2(out_2), .in_1(rot4_1_out_2));
endmodule
