// Logisim project ex2.circ as structural Verilog: 1 circuit, main circuit compute_BrUn
module compute_BrUn (
  input  [31:0] INSTRUCTION,
  output BrUn
);

  wire comparator_1_eq, comparator_2_eq;
  wire [2:0] and_1_out, and_2_out, or_2_out;
  wire [14:12] undriven;

  Comparator #(.mode("unsigned"), .width(3)) comparator_1 (
    .a(3'b111), .b(INSTRUCTION[14:12]), .eq(comparator_1_eq));  // open: gt, lt
  Comparator #(.mode("unsigned"), .width(3)) comparator_2 (
    .a(INSTRUCTION[14:12]), .b(3'b110), .eq(comparator_2_eq));  // open: gt, lt
  assign and_1_out = undriven;  // AND_Gate and_1, 3 bits wide AND_Gate
  or or_1 (BrUn, comparator_1_eq, comparator_2_eq);
  assign and_2_out = undriven;  // AND_Gate and_2, 3 bits wide AND_Gate
  // OR_Gate or_2 has open pins: out=or_2_out
endmodule
